# Fritzing sketch c2 (saved by Fritzing 0.9.3b)
breadboards: 1

parts:
  Raspberry_Pi_1 = Raspberry Pi 3 [part_number=RPI-3-V1.2]
  LED1 = LED - 5mm [color="Red (633nm)" package="5 mm [THT]"]
  R3 = Resistor [tolerance=±5% resistance=220 package=THT]
  R4 = Resistor [tolerance=±5% resistance=220 package=THT]
  S1 = Pushbutton [package="[THT]"]

nets:
  N1: Raspberry_Pi_1.3V3, R4.Pin_0
  N2: Raspberry_Pi_1.GPIO23, S1.Pin_1, S1.Pin_2
  N3: Raspberry_Pi_1.GND, LED1.cathode
  N4: Raspberry_Pi_1.GPIO18, R3.Pin_1
  N5: LED1.anode, R3.Pin_0
  N6: R4.Pin_1, S1.Pin_3, S1.Pin_4

notes:
  Circuito 2
